// Logisim project control-logic.circ as structural Verilog: 1 circuit, main circuit control_logic
module control_logic (
  input  [31:0] Instruction,
  input  BrEq,
  input  BrLt,
  output PCSel,
  output RegWEn,
  output [2:0] ImmSel,
  output BrUn,
  output ASel,
  output BSel,
  output [3:0] ALUSel,
  output MemWEn,
  output [1:0] WBSel
);

  wire and_1_out, and_2_out, and_3_out, and_4_out, and_5_out, and_6_out, and_7_out, and_8_out, and_9_out,
       and_10_out, and_11_out, and_12_out, and_25_out, and_26_out, and_27_out, comparator_1_eq,
       comparator_2_eq, comparator_3_eq, comparator_4_eq, comparator_5_eq, comparator_6_eq, comparator_7_eq,
       comparator_8_eq, comparator_9_eq, comparator_10_eq, comparator_11_eq, comparator_12_eq,
       comparator_13_eq, comparator_14_eq, comparator_15_eq, comparator_16_eq, comparator_17_eq,
       comparator_18_eq, comparator_19_eq, comparator_20_eq, comparator_21_eq, comparator_22_eq,
       comparator_23_eq, comparator_24_eq, comparator_26_eq, comparator_27_eq, comparator_28_eq,
       comparator_29_eq, comparator_30_eq, comparator_31_eq, comparator_32_eq, comparator_33_eq,
       comparator_34_eq, comparator_35_eq, comparator_36_eq, is_add, is_addi, is_and, is_andi, is_I_type,
       is_lb, is_lh, is_lw, is_mul, is_mulh, is_mulhu, is_or, is_ori, is_R_type, is_sll, is_slli, is_slt,
       is_slti, is_sra, is_srai, is_srl, is_srli, is_sub, is_xor, is_xori;
  wire [5:0] ROMInput;
  wire [15:14] rom_1_data;

  ROM #(.addrWidth(6), .dataWidth(16)) rom_1 (
    .addr(ROMInput), .data({rom_1_data, WBSel, MemWEn, ALUSel, BSel, ASel, BrUn, ImmSel, RegWEn}));
  Priority_Encoder #(.select_enc(6)) priority_encoder_1 (
    .in0(is_add), .in1(is_mul), .in2(is_sub), .in3(is_sll), .in4(is_mulh), .in5(is_mulhu), .in6(is_slt),
    .in7(is_xor), .in8(is_srl), .in9(is_sra), .in10(is_or), .in11(is_and), .in12(is_lb), .in13(is_lw),
    .in14(is_lh), .in15(is_addi), .in16(is_slli), .in17(is_slti), .in18(is_xori), .in19(is_srli),
    .in20(is_srai), .in21(is_ori), .in22(is_andi), .out(ROMInput));  // open: in23, in24, in25, in26, in27, in28, in29, in30, in31, in32, in33, in34, in35, in36, in37, in38, in39, in40, in41, in42, in43, in44, in45, in46, in47, in48, in49, in50, in51, in52, in53, in54, in55, in56, in57, in58, in59, in60, in61, in62, in63, gs, en_out, en_in
  Comparator #(.width(3)) comparator_1 (.a(3'b000), .b(Instruction[14:12]), .eq(comparator_1_eq));  // open: gt, lt
  Comparator #(.width(3)) comparator_2 (.a(3'b000), .b(Instruction[14:12]), .eq(comparator_2_eq));  // open: gt, lt
  Comparator #(.width(3)) comparator_3 (.a(3'b000), .b(Instruction[14:12]), .eq(comparator_3_eq));  // open: gt, lt
  Comparator #(.width(3)) comparator_4 (.a(3'b001), .b(Instruction[14:12]), .eq(comparator_4_eq));  // open: gt, lt
  Comparator #(.width(3)) comparator_5 (.a(3'b001), .b(Instruction[14:12]), .eq(comparator_5_eq));  // open: gt, lt
  Comparator #(.width(3)) comparator_6 (.a(3'b011), .b(Instruction[14:12]), .eq(comparator_6_eq));  // open: gt, lt
  Comparator #(.width(3)) comparator_7 (.a(3'b010), .b(Instruction[14:12]), .eq(comparator_7_eq));  // open: gt, lt
  Comparator #(.width(3)) comparator_8 (.a(3'b100), .b(Instruction[14:12]), .eq(comparator_8_eq));  // open: gt, lt
  Comparator #(.width(3)) comparator_9 (.a(3'b101), .b(Instruction[14:12]), .eq(comparator_9_eq));  // open: gt, lt
  Comparator #(.width(3)) comparator_10 (.a(3'b101), .b(Instruction[14:12]), .eq(comparator_10_eq));  // open: gt, lt
  Comparator #(.width(3)) comparator_11 (.a(3'b110), .b(Instruction[14:12]), .eq(comparator_11_eq));  // open: gt, lt
  Comparator #(.width(3)) comparator_12 (.a(3'b111), .b(Instruction[14:12]), .eq(comparator_12_eq));  // open: gt, lt
  Comparator #(.width(7)) comparator_13 (.a({7{1'b0}}), .b(Instruction[31:25]), .eq(comparator_13_eq));  // open: gt, lt
  and and_1 (and_1_out, is_R_type, comparator_1_eq);
  Comparator #(.width(7)) comparator_14 (
    .a(7'b0000001), .b(Instruction[31:25]), .eq(comparator_14_eq));  // open: gt, lt
  and and_2 (and_2_out, is_R_type, comparator_2_eq);
  Comparator #(.width(7)) comparator_15 (
    .a(7'b0100000), .b(Instruction[31:25]), .eq(comparator_15_eq));  // open: gt, lt
  and and_3 (and_3_out, is_R_type, comparator_3_eq);
  Comparator #(.width(7)) comparator_16 (.a({7{1'b0}}), .b(Instruction[31:25]), .eq(comparator_16_eq));  // open: gt, lt
  and and_4 (and_4_out, is_R_type, comparator_4_eq);
  Comparator #(.width(7)) comparator_17 (
    .a(7'b0000001), .b(Instruction[31:25]), .eq(comparator_17_eq));  // open: gt, lt
  and and_5 (and_5_out, is_R_type, comparator_5_eq);
  Comparator #(.width(7)) comparator_18 (
    .a(7'b0000001), .b(Instruction[31:25]), .eq(comparator_18_eq));  // open: gt, lt
  and and_6 (and_6_out, is_R_type, comparator_6_eq);
  Comparator #(.width(7)) comparator_19 (.a({7{1'b0}}), .b(Instruction[31:25]), .eq(comparator_19_eq));  // open: gt, lt
  and and_7 (and_7_out, is_R_type, comparator_7_eq);
  Comparator #(.width(7)) comparator_20 (.a({7{1'b0}}), .b(Instruction[31:25]), .eq(comparator_20_eq));  // open: gt, lt
  and and_8 (and_8_out, is_R_type, comparator_8_eq);
  Comparator #(.width(7)) comparator_21 (.a({7{1'b0}}), .b(Instruction[31:25]), .eq(comparator_21_eq));  // open: gt, lt
  and and_9 (and_9_out, is_R_type, comparator_9_eq);
  Comparator #(.width(7)) comparator_22 (
    .a(7'b0100000), .b(Instruction[31:25]), .eq(comparator_22_eq));  // open: gt, lt
  and and_10 (and_10_out, is_R_type, comparator_10_eq);
  Comparator #(.width(7)) comparator_23 (.a({7{1'b0}}), .b(Instruction[31:25]), .eq(comparator_23_eq));  // open: gt, lt
  and and_11 (and_11_out, is_R_type, comparator_11_eq);
  Comparator #(.width(7)) comparator_24 (.a({7{1'b0}}), .b(Instruction[31:25]), .eq(comparator_24_eq));  // open: gt, lt
  and and_12 (and_12_out, is_R_type, comparator_12_eq);
  Comparator #(.width(7)) comparator_25 (.a(7'b0110011), .b(Instruction[6:0]), .eq(is_R_type));  // open: gt, lt
  and and_13 (is_add, comparator_13_eq, and_1_out);
  and and_14 (is_mul, comparator_14_eq, and_2_out);
  and and_15 (is_sub, comparator_15_eq, and_3_out);
  and and_16 (is_sll, comparator_16_eq, and_4_out);
  and and_17 (is_mulh, comparator_17_eq, and_5_out);
  and and_18 (is_mulhu, comparator_18_eq, and_6_out);
  and and_19 (is_slt, comparator_19_eq, and_7_out);
  and and_20 (is_xor, comparator_20_eq, and_8_out);
  and and_21 (is_srl, comparator_21_eq, and_9_out);
  and and_22 (is_sra, comparator_22_eq, and_10_out);
  and and_23 (is_or, comparator_23_eq, and_11_out);
  and and_24 (is_and, comparator_24_eq, and_12_out);
  Comparator #(.width(3)) comparator_26 (.a(3'b001), .b(Instruction[14:12]), .eq(comparator_26_eq));  // open: gt, lt
  Comparator #(.width(3)) comparator_27 (.a(3'b101), .b(Instruction[14:12]), .eq(comparator_27_eq));  // open: gt, lt
  Comparator #(.width(3)) comparator_28 (.a(3'b101), .b(Instruction[14:12]), .eq(comparator_28_eq));  // open: gt, lt
  Comparator #(.width(7)) comparator_29 (.a({7{1'b0}}), .b(Instruction[31:25]), .eq(comparator_29_eq));  // open: gt, lt
  and and_25 (and_25_out, is_I_type, comparator_26_eq);
  Comparator #(.width(7)) comparator_30 (.a({7{1'b0}}), .b(Instruction[31:25]), .eq(comparator_30_eq));  // open: gt, lt
  and and_26 (and_26_out, is_I_type, comparator_27_eq);
  Comparator #(.width(7)) comparator_31 (
    .a(7'b0100000), .b(Instruction[31:25]), .eq(comparator_31_eq));  // open: gt, lt
  and and_27 (and_27_out, is_I_type, comparator_28_eq);
  Comparator #(.width(3)) comparator_32 (.a(3'b000), .b(Instruction[14:12]), .eq(comparator_32_eq));  // open: gt, lt
  and and_28 (is_slli, comparator_29_eq, and_25_out);
  Comparator #(.width(3)) comparator_33 (.a(3'b010), .b(Instruction[14:12]), .eq(comparator_33_eq));  // open: gt, lt
  Comparator #(.width(3)) comparator_34 (.a(3'b100), .b(Instruction[14:12]), .eq(comparator_34_eq));  // open: gt, lt
  and and_29 (is_srli, comparator_30_eq, and_26_out);
  and and_30 (is_srai, comparator_31_eq, and_27_out);
  Comparator #(.width(3)) comparator_35 (.a(3'b110), .b(Instruction[14:12]), .eq(comparator_35_eq));  // open: gt, lt
  Comparator #(.width(3)) comparator_36 (.a(3'b111), .b(Instruction[14:12]), .eq(comparator_36_eq));  // open: gt, lt
  Comparator #(.width(7)) comparator_37 (.a(7'b0010011), .b(Instruction[6:0]), .eq(is_I_type));  // open: gt, lt
  and and_31 (is_addi, is_I_type, comparator_32_eq);
  and and_32 (is_slti, is_I_type, comparator_33_eq);
  and and_33 (is_xori, is_I_type, comparator_34_eq);
  and and_34 (is_ori, is_I_type, comparator_35_eq);
  and and_35 (is_andi, is_I_type, comparator_36_eq);

  assign PCSel = 1'b0;

  // Notes on the sheet:
  //   INPUTS to your circuit
  //   contents of rom_1 (hex, n*v repeats v):
  //   1001 1401 1601 1081 1481 1581 1101 1201 1281 1681 1301 1381 0 0 0 1041 10c1 1141 1241 12c1 16c1 1341
  //   13c1
  //   ROM FOR CONTROL LOGIC
  //   DON'T CHANGE THE LOCATIONS OF THE INPUTS AND OUTPUTS!
  //   This is only if you choose to do the ROM option
  //   OUTPUT from your circuit
endmodule
